// Logisim project spi.circ as structural Verilog: 3 circuits, main circuit main
module main (
  input  RESET,
  input  [3:0] D8_11,
  input  [7:0] D0_7,
  input  view_shreg,
  output [7:0] DATA_OUT
);

  wire and_1_out, and_2_out, CLK_out, CLK_x2_out, CTR_pin3, CTR_pin4, CTR_pin5, CTR_pin6, CTR_pin10,
       CTR_pin15, INHIBIT_out, or_1_out, shift_register_1_p1, shift_register_1_p4, SHREG_pin17, spi_1_clk_d2,
       spi_1_ls163_clk, spi_1_ls163_clr, spi_1_ls163_enp, spi_1_ls163_load, spi_1_ls299_clk,
       spi_1_ls299_nclr, spi_1_ls299_noe1, spi_1_ls299_noe2, spi_1_ls299_s0, spi_1_ls299_s1, spi_1_ls299_sr,
       spi_1_mosi, spi_1_spi_clk, STATE_MACHINE_data, STATE_MACHINE_rw, STATE_MACHINE_spi_en,
       STATE_MACHINE_uds;
  wire [3:0] transistor_2_out;

  Clock #(.highDuration(2), .lowDuration(2)) CLK (.out(CLK_out));
  Clock CLK_x2 (.out(CLK_x2_out));
  Button #(.press("passive")) INHIBIT (.out(INHIBIT_out));
  stateMachine STATE_MACHINE (
    .RESET(RESET), .CLK_d2(spi_1_clk_d2), .CLK(CLK_out), .CLK_x2(CLK_x2_out), .INHIBIT(INHIBIT_out),
    .SPI_EN(STATE_MACHINE_spi_en), .RW(STATE_MACHINE_rw), .UDS(STATE_MACHINE_uds), .DATA(STATE_MACHINE_data));
  and and_1 (and_1_out, STATE_MACHINE_spi_en, ~view_shreg);  // AND_Gate
  or or_1 (or_1_out, STATE_MACHINE_rw, view_shreg);
  and and_2 (and_2_out, STATE_MACHINE_uds, ~view_shreg);  // AND_Gate
  Transistor #(.width(8)) transistor_1 (.in(D0_7), .out(DATA_OUT), .gate(STATE_MACHINE_data));
  Transistor #(.width(4)) transistor_2 (.in(D8_11), .out(transistor_2_out), .gate(STATE_MACHINE_data));
  Pull_Resistor pull_resistor_1 (.node(transistor_2_out));
  Pull_Resistor pull_resistor_2 (.node(DATA_OUT));
  spi spi_1 (
    .RESET(RESET), .SPI_EN(and_1_out), .R_W(or_1_out), .UDS(and_2_out), .MISO(shift_register_1_p4),
    .LS163_RCO(CTR_pin15), .LS299_QHp(SHREG_pin17), .CLK_d2(spi_1_clk_d2), .SPI_CLK(spi_1_spi_clk),
    .MOSI(spi_1_mosi), .LS163_CLR(spi_1_ls163_clr), .LS163_LOAD(spi_1_ls163_load), .LS299_S1(spi_1_ls299_s1),
    .LS299_CLK(spi_1_ls299_clk), .LS299_SR(spi_1_ls299_sr), .LS163_CLK(spi_1_ls163_clk),
    .LS163_EnP(spi_1_ls163_enp), .LS299_S0(spi_1_ls299_s0), .LS299_nOE1(spi_1_ls299_noe1),
    .LS299_nOE2(spi_1_ls299_noe2), .LS299_nCLR(spi_1_ls299_nclr));
  _74163 #(.ShowInternalStructure("true")) CTR (
    .pin1(spi_1_ls163_clr), .pin2(spi_1_ls163_clk), .pin3(CTR_pin3), .pin4(CTR_pin4), .pin5(CTR_pin5),
    .pin6(CTR_pin6), .pin7(spi_1_ls163_enp), .pin15(CTR_pin15), .pin10(CTR_pin10), .pin9(spi_1_ls163_load));  // open: pin14, pin13, pin12, pin11
  _74299 #(.ShowInternalStructure("true")) SHREG (
    .pin1(spi_1_ls299_s0), .pin2(spi_1_ls299_noe1), .pin3(spi_1_ls299_noe2), .pin4(DATA_OUT[6]),
    .pin5(DATA_OUT[4]), .pin6(DATA_OUT[2]), .pin7(DATA_OUT[0]), .pin9(spi_1_ls299_nclr),
    .pin19(spi_1_ls299_s1), .pin17(SHREG_pin17), .pin16(DATA_OUT[7]), .pin15(DATA_OUT[5]),
    .pin14(DATA_OUT[3]), .pin13(DATA_OUT[1]), .pin12(spi_1_ls299_clk), .pin11(spi_1_ls299_sr));  // open: pin8, pin18
  // Shift_Register shift_register_1: pin names not known; wires that end beside it: shift_register_1_p1, spi_1_spi_clk, spi_1_mosi, shift_register_1_p4
  not not_1 (shift_register_1_p1, RESET);
  // also tied to GND on the sheet: {CTR_pin3, CTR_pin6}
  // also tied to VCC on the sheet: {CTR_pin4, CTR_pin5, CTR_pin10}

  // Notes on the sheet:
  //   D8_11: initial=0x7
  //   D0_7: initial=0xaa
  //   RESET: initial=0x1
endmodule

module stateMachine (
  input  RESET,
  input  CLK_d2,
  input  CLK,
  input  CLK_x2,
  input  INHIBIT,
  output SPI_EN,
  output RW,
  output UDS,
  output DATA
);

  wire and_1_out, and_2_out, and_3_out, or_1_out, or_2_out, shift_register_1_p3, shift_register_1_p4,
       shift_register_1_p5, shift_register_1_p6, shift_register_1_p7, shift_register_1_p8,
       shift_register_1_p9, shift_register_1_p10;
  wire [7:0] undriven;

  or or_1 (or_1_out, and_1_out, and_3_out, and_2_out);
  and and_1 (and_1_out, undriven[0], INHIBIT);
  and and_2 (and_2_out, CLK_x2, RESET);
  // Shift_Register #(.length(15)) shift_register_1: pin names not known; wires that end beside it: 1'b1, or_1_out, shift_register_1_p3, shift_register_1_p4, shift_register_1_p5, shift_register_1_p6, shift_register_1_p7, shift_register_1_p8, shift_register_1_p9, shift_register_1_p10, undriven[1], undriven[2], undriven[3], undriven[4]
  and and_3 (and_3_out, ~CLK, ~CLK_d2, undriven[7]);  // AND_Gate
  nor nor_1 (shift_register_1_p3, shift_register_1_p4, shift_register_1_p5, shift_register_1_p6, shift_register_1_p7, shift_register_1_p8, shift_register_1_p9, shift_register_1_p10, or_2_out);
  or or_2 (or_2_out, undriven[0], undriven[1], undriven[2], undriven[3], undriven[4], undriven[5], undriven[6], undriven[7], 1'b0);
  nor nor_2 (SPI_EN, shift_register_1_p4, shift_register_1_p5, shift_register_1_p6, shift_register_1_p7, shift_register_1_p8, shift_register_1_p9, shift_register_1_p10);
  nor nor_3 (RW, shift_register_1_p5, shift_register_1_p6, shift_register_1_p7, shift_register_1_p8, shift_register_1_p9, shift_register_1_p10);
  nor nor_4 (UDS, shift_register_1_p7, shift_register_1_p8);
  nor nor_5 (DATA, shift_register_1_p6, shift_register_1_p7, shift_register_1_p8, shift_register_1_p9);

  // Notes on the sheet:
  //   RESET: initial=0x1
endmodule

module spi (
  input  RESET,
  input  SPI_EN,
  input  R_W,
  input  UDS,
  input  MISO,
  input  LS163_RCO,
  input  LS299_QHp,
  output CLK_d2,
  output SPI_CLK,
  output MOSI,
  output LS163_CLR,
  output LS163_LOAD,
  output LS299_S1,
  output LS299_CLK,
  output LS299_SR,
  output LS163_CLK,
  output LS163_EnP,
  output LS299_S0,
  output LS299_nOE1,
  output LS299_nOE2,
  output LS299_nCLR
);

  wire CLK_DIV_q, CLK_out, nor_1_out, not_3_out;

  Clock #(.highDuration(2), .lowDuration(2)) CLK (.out(CLK_out));
  D_Flip_Flop #(.trigger("falling")) CLK_DIV (
    .D(CLK_d2), .clk(CLK_out), .Q(CLK_DIV_q), .Qn(CLK_d2));  // open: preset, reset
  or or_1 (LS163_LOAD, UDS, SPI_EN);
  not not_1 (LS163_EnP, LS163_RCO);
  nor nor_1 (nor_1_out, CLK_DIV_q, ~RESET, LS163_RCO);  // NOR_Gate
  not not_2 (LS299_nOE1, R_W);
  nor nor_2 (LS299_S1, SPI_EN, R_W);
  and and_1 (LS299_CLK, LS163_LOAD, nor_1_out);
  not not_3 (not_3_out, CLK_out);
  and and_2 (SPI_CLK, SPI_EN, LS299_CLK);
  D_Flip_Flop d_ff_1 (.D(LS299_QHp), .clk(not_3_out), .Q(MOSI));  // open: Qn, preset, reset

  assign LS163_CLK = CLK_d2;
  assign LS163_CLR = RESET;
  assign LS299_nCLR = RESET;
  assign LS299_nOE2 = SPI_EN;
  assign LS299_S0 = 1'b1;
  assign LS299_SR = MISO;

  // Notes on the sheet:
  //   RESET: initial=0x1
  //   SPI_EN: initial=0x1
  //   R_W: initial=0x1
  //   UDS: initial=0x1
endmodule
